# Fritzing sketch CircuitController (saved by Fritzing 0.9.3b)
breadboards: 1

parts:
  WeMos_D1_Mini3 = WeMos D1 Mini  # not connected
  DS2 = DS18B20 1-Wire Temperature Sensor [part_number=DS18B20]
  R2 = Resistor [tolerance=±5% resistance=220 package="0402 [SMD]"]
  U2 = mystery part, 3 pins [chip_label="433,97MHz TX"]

nets:
  N1: DS2.GND, U2.pin3
  N2: DS2.DQ, R2.Pin_0
  N3: DS2.VDD, R2.Pin_1, U2.pin2
